// Logisim project MINIRAM.circ as structural Verilog: 1 circuit, main circuit main
module main (
  input  in_1,
  input  in_2,
  input  in_3,
  input  in_4,
  input  in_5,
  input  in_6,
  input  in_7,
  input  in_8,
  input  in_9,
  input  in_10,
  input  in_11,
  input  in_12,
  input  in_13,
  input  in_14,
  input  in_15,
  input  in_16,
  input  in_17,
  input  in_18,
  input  in_19,
  input  in_20,
  input  in_21,
  input  in_22,
  input  in_23,
  input  in_24,
  input  in_25,
  input  in_26,
  input  in_27,
  input  in_28,
  input  in_29,
  input  in_30,
  input  in_31,
  output out_32,
  output out_33,
  output out_34,
  output out_35,
  output out_36,
  output out_37,
  output out_38,
  output out_39,
  output out_40,
  output out_41,
  output out_42,
  output out_43,
  output out_44,
  output out_45,
  output out_46,
  output out_47,
  output out_48,
  output out_49,
  output out_50,
  output out_51,
  output out_52,
  output out_53,
  output out_54,
  output out_55
);

  wire and_1_out, and_2_out, and_3_out, and_4_out, and_5_out, and_6_out, and_7_out, and_8_out, and_9_out,
       and_10_out, and_11_out, and_12_out, and_13_out, and_14_out, and_15_out, and_16_out, and_21_out,
       and_22_out, and_24_out, and_25_out, and_26_out, and_28_out, and_29_out, and_30_out, and_31_out,
       and_32_out, and_33_out, and_34_out, and_35_out, and_36_out, and_37_out, and_38_out, and_39_out,
       and_40_out, and_41_out, and_42_out, and_43_out, and_44_out, and_45_out, and_46_out, and_47_out,
       and_48_out, and_49_out, and_50_out, and_51_out, and_52_out, and_53_out, and_54_out, and_55_out,
       and_56_out, and_57_out, and_58_out, and_59_out, and_60_out, and_61_out, and_62_out, and_63_out,
       and_64_out, and_65_out, and_66_out, and_67_out, and_68_out, and_69_out, and_70_out, and_71_out,
       and_72_out, and_73_out, and_74_out, and_75_out, and_76_out, not_1_out, not_2_out, not_3_out,
       not_4_out, not_5_out, not_6_out, not_7_out, not_8_out, not_9_out, not_10_out, or_1_out, or_2_out,
       or_3_out, or_4_out, or_5_out, or_6_out, or_7_out, or_8_out, or_9_out, or_10_out, or_11_out, or_12_out,
       or_13_out, or_14_out, or_15_out, or_16_out, or_17_out, or_18_out, or_19_out, or_20_out, or_21_out,
       or_22_out, or_23_out, or_24_out, s_r_ff_1_q, s_r_ff_2_q, s_r_ff_3_q, s_r_ff_4_q, s_r_ff_5_q,
       s_r_ff_6_q, s_r_ff_7_q;

  S_R_Flip_Flop s_r_ff_1 (.Q(s_r_ff_1_q));  // open: S, clk, R, Qn, preset, reset, en
  S_R_Flip_Flop s_r_ff_2 (.Q(s_r_ff_2_q));  // open: S, clk, R, Qn, preset, reset, en
  S_R_Flip_Flop s_r_ff_3 (.Q(s_r_ff_3_q));  // open: S, clk, R, Qn, preset, reset, en
  not not_1 (not_1_out, in_5);
  and and_1 (and_1_out, out_35, not_1_out);
  and and_2 (and_2_out, in_5, in_7);
  and and_3 (and_3_out, out_38, not_1_out);
  and and_4 (and_4_out, in_5, in_9);
  and and_5 (and_5_out, out_41, not_1_out);
  and and_6 (and_6_out, in_5, in_13);
  and and_7 (and_7_out, out_43, not_1_out);
  and and_8 (and_8_out, in_5, in_14);
  not not_2 (not_2_out, or_21_out);
  not not_3 (not_3_out, or_22_out);
  not not_4 (not_4_out, or_23_out);
  not not_5 (not_5_out, or_24_out);
  not not_6 (not_6_out, s_r_ff_3_q);
  or or_1 (or_1_out, and_1_out, and_2_out);
  or or_2 (or_2_out, and_3_out, and_4_out);
  or or_3 (or_3_out, and_5_out, and_6_out);
  or or_4 (or_4_out, and_7_out, and_8_out);
  and and_9 (and_9_out, or_21_out, not_6_out);
  and and_10 (and_10_out, not_2_out, not_6_out);
  and and_11 (and_11_out, or_22_out, not_6_out);
  and and_12 (and_12_out, not_3_out, not_6_out);
  and and_13 (and_13_out, or_23_out, not_6_out);
  and and_14 (and_14_out, not_4_out, not_6_out);
  and and_15 (and_15_out, or_24_out, not_6_out);
  and and_16 (and_16_out, not_5_out, not_6_out);
  D_Flip_Flop d_ff_1 (.clk(in_4), .D(or_1_out), .Q(out_35));  // open: Qn, preset, en, reset
  D_Flip_Flop d_ff_2 (.clk(in_4), .D(or_2_out), .Q(out_38));  // open: Qn, preset, en, reset
  D_Flip_Flop d_ff_3 (.clk(in_4), .D(or_3_out), .Q(out_41));  // open: Qn, preset, en, reset
  D_Flip_Flop d_ff_4 (.clk(in_4), .D(or_4_out), .Q(out_43));  // open: Qn, preset, en, reset
  S_R_Flip_Flop s_r_ff_4 (.S(and_9_out), .clk(and_10_out), .R(in_27), .Q(s_r_ff_4_q));  // open: Qn, preset, reset, en
  S_R_Flip_Flop s_r_ff_5 (.S(and_11_out), .clk(and_12_out), .R(in_27), .Q(s_r_ff_5_q));  // open: Qn, preset, reset, en
  S_R_Flip_Flop s_r_ff_6 (.S(and_13_out), .clk(and_14_out), .R(in_27), .Q(s_r_ff_6_q));  // open: Qn, preset, reset, en
  S_R_Flip_Flop s_r_ff_7 (.S(and_15_out), .clk(and_16_out), .R(in_27), .Q(s_r_ff_7_q));  // open: Qn, preset, reset, en
  and and_17 (out_34, not_1_out, out_35);
  and and_18 (out_37, not_1_out, out_38);
  and and_19 (out_40, not_1_out, out_41);
  and and_20 (out_42, not_1_out, out_43);
  and and_21 (and_21_out, s_r_ff_4_q, s_r_ff_3_q);
  and and_22 (and_22_out, s_r_ff_5_q, s_r_ff_3_q);
  and and_23 (and_22_out, s_r_ff_6_q, s_r_ff_3_q);
  and and_24 (and_24_out, s_r_ff_7_q, s_r_ff_3_q);
  and and_25 (and_25_out, s_r_ff_1_q, s_r_ff_2_q);
  and and_26 (and_26_out, s_r_ff_1_q, s_r_ff_2_q);
  and and_27 (in_21, s_r_ff_1_q, s_r_ff_2_q);
  and and_28 (and_28_out, s_r_ff_1_q, s_r_ff_2_q);
  not not_7 (not_7_out, in_2);
  not not_8 (not_8_out, in_12);
  not not_9 (not_9_out, in_20);
  not not_10 (not_10_out, in_26);
  and and_29 (and_29_out, out_52, not_10_out);
  and and_30 (and_30_out, in_26, in_28);
  and and_31 (and_31_out, out_53, not_10_out);
  and and_32 (and_32_out, in_26, in_29);
  and and_33 (and_33_out, out_54, not_10_out);
  and and_34 (and_34_out, in_26, in_30);
  and and_35 (and_35_out, out_55, not_10_out);
  and and_36 (and_36_out, in_26, in_31);
  and and_37 (and_37_out, out_32, not_7_out);
  and and_38 (and_38_out, in_2, in_3);
  and and_39 (and_39_out, out_33, and_22_out);
  and and_40 (and_40_out, in_2, in_6);
  and and_41 (and_41_out, out_36, and_22_out);
  and and_42 (and_42_out, in_2, in_8);
  and and_43 (and_43_out, out_39, and_22_out);
  and and_44 (and_44_out, in_2, in_10);
  and and_45 (and_45_out, out_44, not_8_out);
  and and_46 (and_46_out, in_12, in_15);
  and and_47 (and_47_out, out_45, not_8_out);
  and and_48 (and_48_out, in_12, in_16);
  and and_49 (and_49_out, out_46, not_8_out);
  and and_50 (and_50_out, in_12, in_17);
  and and_51 (and_51_out, out_47, not_8_out);
  and and_52 (and_52_out, in_12, in_18);
  and and_53 (and_53_out, out_48, not_9_out);
  and and_54 (and_54_out, in_20, in_21);
  and and_55 (and_55_out, out_49, not_9_out);
  and and_56 (and_56_out, in_20, in_22);
  and and_57 (and_57_out, out_50, not_9_out);
  and and_58 (and_58_out, in_20, in_23);
  and and_59 (and_59_out, out_51, not_9_out);
  and and_60 (and_60_out, in_20, in_24);
  or or_5 (or_5_out, and_37_out, and_38_out);
  or or_6 (or_6_out, and_39_out, and_40_out);
  or or_7 (or_7_out, and_41_out, and_42_out);
  or or_8 (or_8_out, and_43_out, and_44_out);
  or or_9 (or_9_out, and_45_out, and_46_out);
  or or_10 (or_10_out, and_47_out, and_48_out);
  or or_11 (or_11_out, and_49_out, and_50_out);
  or or_12 (or_12_out, and_51_out, and_52_out);
  or or_13 (or_13_out, and_53_out, and_54_out);
  or or_14 (or_14_out, and_55_out, and_56_out);
  or or_15 (or_15_out, and_57_out, and_58_out);
  or or_16 (or_16_out, and_59_out, and_60_out);
  or or_17 (or_17_out, and_29_out, and_30_out);
  or or_18 (or_18_out, and_31_out, and_32_out);
  or or_19 (or_19_out, and_33_out, and_34_out);
  or or_20 (or_20_out, and_35_out, and_36_out);
  D_Flip_Flop d_ff_5 (.clk(in_1), .D(or_5_out), .Q(out_32), .preset(and_25_out));  // open: Qn, en, reset
  D_Flip_Flop d_ff_6 (.clk(in_1), .D(or_6_out), .Q(out_33));  // open: Qn, preset, en, reset
  D_Flip_Flop d_ff_7 (.clk(in_1), .D(or_7_out), .Q(out_36));  // open: Qn, preset, en, reset
  D_Flip_Flop d_ff_8 (.clk(in_1), .D(or_8_out), .Q(out_39));  // open: Qn, preset, en, reset
  D_Flip_Flop d_ff_9 (.clk(in_11), .D(or_9_out), .Q(out_44), .preset(and_26_out));  // open: Qn, en, reset
  D_Flip_Flop d_ff_10 (.clk(in_11), .D(or_10_out), .Q(out_45));  // open: Qn, preset, en, reset
  D_Flip_Flop d_ff_11 (.clk(in_11), .D(or_11_out), .Q(out_46));  // open: Qn, preset, en, reset
  D_Flip_Flop d_ff_12 (.clk(in_11), .D(or_12_out), .Q(out_47));  // open: Qn, preset, en, reset
  D_Flip_Flop d_ff_13 (.clk(in_19), .D(or_13_out), .Q(out_48), .preset(in_21));  // open: Qn, en, reset
  D_Flip_Flop d_ff_14 (.clk(in_19), .D(or_14_out), .Q(out_49));  // open: Qn, preset, en, reset
  D_Flip_Flop d_ff_15 (.clk(in_19), .D(or_15_out), .Q(out_50));  // open: Qn, preset, en, reset
  D_Flip_Flop d_ff_16 (.clk(in_19), .D(or_16_out), .Q(out_51));  // open: Qn, preset, en, reset
  D_Flip_Flop d_ff_17 (.clk(in_25), .D(or_17_out), .Q(out_52), .preset(and_28_out));  // open: Qn, en, reset
  D_Flip_Flop d_ff_18 (.clk(in_25), .D(or_18_out), .Q(out_53));  // open: Qn, preset, en, reset
  D_Flip_Flop d_ff_19 (.clk(in_25), .D(or_19_out), .Q(out_54));  // open: Qn, preset, en, reset
  D_Flip_Flop d_ff_20 (.clk(in_25), .D(or_20_out), .Q(out_55));  // open: Qn, preset, en, reset
  and and_61 (and_61_out, not_7_out, out_32);
  and and_62 (and_62_out, not_7_out, out_33);
  and and_63 (and_63_out, not_7_out, out_36);
  and and_64 (and_64_out, not_7_out, out_39);
  and and_65 (and_65_out, not_8_out, out_44);
  and and_66 (and_66_out, not_8_out, out_45);
  and and_67 (and_67_out, not_8_out, out_46);
  and and_68 (and_68_out, not_8_out, out_47);
  and and_69 (and_69_out, not_9_out, out_48);
  and and_70 (and_70_out, not_9_out, out_49);
  and and_71 (and_71_out, not_9_out, out_50);
  and and_72 (and_72_out, not_9_out, out_51);
  and and_73 (and_73_out, not_10_out, out_52);
  and and_74 (and_74_out, not_10_out, out_53);
  and and_75 (and_75_out, not_10_out, out_54);
  and and_76 (and_76_out, not_10_out, out_55);
  or or_21 (or_21_out, and_65_out, and_61_out, and_69_out, and_73_out);
  or or_22 (or_22_out, and_62_out, and_70_out, and_74_out, and_66_out);
  or or_23 (or_23_out, and_63_out, and_67_out, and_75_out, and_71_out);
  or or_24 (or_24_out, and_64_out, and_68_out, and_72_out, and_76_out);
endmodule
