// Logisim project Four_Bits_Add_Sub.circ as structural Verilog: 2 circuits, main circuit Add_Sub_4Bits
module Add_Sub_4Bits (
  input  [3:0] A,
  input  [3:0] B,
  input  Add_Sub,
  output [3:0] R,
  output Zero,
  output Overflow
);

  wire add_1bit_1_cout, add_1bit_2_cout, add_1bit_3_cout, add_1bit_4_cout, not_1_out, not_2_out, not_3_out,
       not_4_out, xor_1_out, xor_2_out, xor_3_out, xor_4_out;

  // Probe on A
  // Probe on B
  xor xor_1 (xor_1_out, Add_Sub, B[0]);
  xor xor_2 (xor_2_out, Add_Sub, B[1]);
  xor xor_3 (xor_3_out, Add_Sub, B[2]);
  xor xor_4 (xor_4_out, Add_Sub, B[3]);
  Add_1Bit add_1bit_1 (.Cout(add_1bit_1_cout), .Sum(R[0]), .B(xor_1_out), .A(A[0]), .Cin(Add_Sub));
  not not_1 (not_1_out, R[1]);
  Add_1Bit add_1bit_2 (.Cout(add_1bit_2_cout), .Sum(R[1]), .B(xor_2_out), .A(A[1]), .Cin(add_1bit_1_cout));
  not not_2 (not_2_out, R[2]);
  Add_1Bit add_1bit_3 (.Cout(add_1bit_3_cout), .Sum(R[2]), .B(xor_3_out), .A(A[2]), .Cin(add_1bit_2_cout));
  Add_1Bit add_1bit_4 (.Cout(add_1bit_4_cout), .Sum(R[3]), .B(xor_4_out), .A(A[3]), .Cin(add_1bit_3_cout));
  // Probe on R
  not not_3 (not_3_out, R[0]);
  not not_4 (not_4_out, R[3]);
  and and_1 (Zero, not_3_out, not_2_out, not_4_out, not_1_out);
  xor xor_5 (Overflow, add_1bit_4_cout, add_1bit_3_cout);

  // Notes on the sheet:
  //   YASSINE MHEDHBI 260673563
  //   MAKE SURE THAT YOU OPENED THIS PROJECT IN "LOGISIM-EVOLUTION"
  //   YOU CAN FIND "LOGISIM-EVOLUTION" PRORAM IN THE ASSIGNMENT'S FOLDER
  //   DO NOT USE "LOGISIM" VERSION TO SOLVE THIS ASSIGNMENT!
endmodule

module Add_1Bit (
  input  Cin,
  input  A,
  input  B,
  output Sum,
  output Cout
);

  wire and_1_out, and_2_out, xor_1_out;

  xor xor_1 (xor_1_out, A, B);
  xor xor_2 (Sum, Cin, xor_1_out);
  and and_1 (and_1_out, Cin, xor_1_out);
  and and_2 (and_2_out, A, B);
  xor xor_3 (Cout, and_1_out, and_2_out);

  // Notes on the sheet:
  //   YASSINE MHEDHBI 260673563
  //   MAKE SURE THAT YOU OPENED THIS PROJECT IN "LOGISIM-EVOLUTION"
  //   YOU CAN FIND "LOGISIM-EVOLUTION" PRORAM IN THE ASSIGNMENT'S FOLDER
  //   DO NOT USE "LOGISIM" VERSION TO SOLVE THIS ASSIGNMENT!
endmodule
